# Fritzing sketch Project_1 (saved by Fritzing 0.9.0b)
circuit board: 7.5cm x 4.5cm
breadboards: 1

parts:
  R3 = Resistor [tolerance=±5% resistance=220 package=THT]
  R4 = Resistor [tolerance=±5% resistance=220 package=THT]
  R2 = Resistor [tolerance=±5% resistance=220 package=THT]
  LED2 = LED - 5mm [color="Red (633nm)" package="5 mm [THT]"]
  J3 = female pin header, 2 pins [form="♀ (female)"]
  LED6 = LED - 5mm [color="Red (633nm)" package="5 mm [THT]"]
  R5 = Resistor [tolerance=±5% resistance=220 package=THT]
  R7 = Resistor [tolerance=±5% resistance=220 package=THT]
  LED4 = LED - 5mm [color="Red (633nm)" package="5 mm [THT]"]
  J5 = female pin header, 2 pins [form="♀ (female)"]
  LED3 = LED - 5mm [color="Red (633nm)" package="5 mm [THT]"]
  LED5 = LED - 5mm [color="Red (633nm)" package="5 mm [THT]"]
  J4 = female pin header, 2 pins [form="♀ (female)"]
  LED7 = LED - 5mm [color="Red (633nm)" package="5 mm [THT]"]
  LED1 = LED - 5mm [color="Red (633nm)" package="5 mm [THT]"]
  R6 = Resistor [tolerance=±5% resistance=220 package=THT]
  R1 = Resistor [tolerance=±5% resistance=220 package=THT]
  74HC595 = 74HC595 [package="DIP16 [THT]"]

nets:
  N1: R3.Pin_0, 74HC595.Q2
  N2: R3.Pin_1, LED3.anode
  N3: R4.Pin_0, 74HC595.Q3
  N4: R4.Pin_1, LED4.anode
  N5: R2.Pin_0, 74HC595.Q1
  N6: R2.Pin_1, LED2.anode
  GND: LED2.cathode, J3.pin2, LED6.cathode, LED4.cathode, LED3.cathode, LED5.cathode, LED7.cathode, LED1.cathode, 74HC595.GND
  N7: J3.pin1, 74HC595.MR, 74HC595.VCC
  N8: LED6.anode, R6.Pin_1
  N9: R5.Pin_0, 74HC595.Q4
  N10: R5.Pin_1, LED5.anode
  N11: R7.Pin_0, 74HC595.Q6
  N12: R7.Pin_1, LED7.anode
  N13: J5.pin1, 74HC595.ST_CP
  N14: J5.pin2, 74HC595.SH_CP
  N15: J4.pin1, 74HC595.DS
  N16: J4.pin2, 74HC595.OE
  N17: LED1.anode, R1.Pin_1
  N18: R6.Pin_0, 74HC595.Q5
  N19: R1.Pin_0, 74HC595.Q0

notes:
  Daniel Hienzsch - R.H.I.
  Gnd
  OE
  DS
  ST
  5v
  SH
  Electronic Dice v1.0
